# Fritzing sketch cart_circuit (saved by Fritzing 0.9.3b)

parts:
  Part1 = Arduino Uno (Rev3)
  VCC1 = Battery block 9V
  M2 = DC Motor
  J1 = Basic Servo
  S2 = H-Bridge with L298N
  M1 = DC Motor

nets:
  N1: Part1.D11_PWM/MOSI, J1.pulse
  N2: Part1.D2, S2.IN1
  N3: Part1.D3_PWM, S2.IN2
  N4: Part1.D4, S2.IN3
  N5: Part1.D5_PWM, S2.ENA
  N6: Part1.D6_PWM, S2.ENB
  N7: Part1.D7, S2.IN4
  VIN: Part1.VIN, S2.5V
  GND: VCC1.-, J1.gnd, S2.GND
  VCC: VCC1.+, J1.vcc, S2.12V
  N8: M2.pin_1, M2.pin_2, S2.M2-01, S2.M2-02
  N9: S2.M1-01, M1.pin_2
  N10: S2.M1-02, M1.pin_1

custom parts:
  H-Bridge with L298N: h-bridge
